# Fritzing sketch hackfest2015 (saved by Fritzing 0.9.2b)
perfboards: 5
breadboards: 1

parts:
  rp01 = Raspberry Pi 2
  ar01 = Arduino Mega 2560 (Rev3)
  casino_(lcd01) = 128 x 64 Graphic LCD
  R1 = Resistor [tolerance=±5% resistance=10k package=THT]
  LED2 = smd LED [color="Red (633nm)" package="0805 [SMD]"]
  R2 = Resistor [tolerance=±5% resistance=330 package=THT]
  pipeline_(lcd02) = 128 x 64 Graphic LCD  # not connected
  ar02 = Arduino Uno (Rev3) - ICSP
  solenoid01 = Solenoid  # not connected
  ar03 = Arduino Uno (Rev3) - ICSP
  VCC1 = Battery  # not connected

nets:
  N1: rp01.GPIO2, ar01.D20/SDA, ar02.A4/SDA, ar03.A4/SDA
  N2: rp01.GPIO3, ar01.D21/SCL, ar02.A5/SCL, ar03.A5/SCL
  GND: rp01.GND, ar01.GND, casino_(lcd01).1_Vss, casino_(lcd01).20_K(-), ar02.GND
  N3: ar01.D13_PWM, casino_(lcd01).6_Enable
  N4: ar01.D12_PWM, casino_(lcd01).5_R/W
  N5: ar01.D11_PWM, casino_(lcd01).4_D/I
  N6: ar01.D10_PWM, casino_(lcd01).3_Vo
  N7: ar01.D9_PWM, R1.Pin_1
  N8: ar01.D3_PWM, R2.Pin_1
  N9: LED2.anode, R2.Pin_0

// code stored in the sketch: test-lcd12864.ino
#include <LiquidCrystal.h>

LiquidCrystal lcd(12, 11, 5, 4, 3, 2);
#define   CONTRAST_PIN 	 10
#define   BACKLIGHT_PIN  9
#define   CONTRAST       125

void setup()
{
  // Switch on the backlight and LCD contrast levels
  pinMode(CONTRAST_PIN, OUTPUT);
  pinMode(BACKLIGHT_PIN, OUTPUT);

  digitalWrite(BACKLIGHT_PIN, HIGH);
  analogWrite (CONTRAST_PIN, CONTRAST);
    
  lcd.begin(128,64);               // initialize the lcd 

  lcd.home ();                   // go home
  lcd.print("Hello, ARDUINO ");  
  lcd.setCursor ( 0, 1 );        // go to the next line
  lcd.print (" WORLD!");      
}

void loop()
{

}
